# Fritzing sketch alco2 (saved by Fritzing 0.9.10b)

parts:
  U1 = ESP32-38PinWide [part_number=ESP32-38PinWide]
  LCD1 = LCD screen
  DS1 = DS18B20 1-Wire Temperature Sensor [part_number=DS18B20]
  LCM1602_IIC1 = LCM1602 IIC [part_number="LCM1602 IIC" chip_label="LCM1602 IIC" package="DIP (Dual Inline) [THT]"]
  M1 = BME280
  R1 = Resistor [tolerance=±5% power=0.25 resistance=220 package=THT]
  R2 = Resistor [tolerance=±5% power=0.25 resistance=220 package=THT]
  LED1 = LED - 5mm [color="Red (633nm)" current=0.030 package="5 mm [THT]"]
  S2 = Pushbutton [package="[SMD]"]
  S3 = Pushbutton [package="[SMD]"]
  S4 = Pushbutton [package="[SMD]"]
  S5 = Pushbutton [package="[SMD]"]
  R3 = Resistor [tolerance=±5% power=0.25 resistance=220 package=THT]
  R4 = Resistor [tolerance=±5% power=0.25 resistance=220 package=THT]
  R5 = Resistor [tolerance=±5% power=0.25 resistance=220 package=THT]
  R6 = Resistor [tolerance=±5% power=0.25 resistance=220 package=THT]  # not connected
  J1 = Piezo Speaker

nets:
  VCC: U1.3.3, LCM1602_IIC1.VCC, M1.VIN, R1.Pin_1
  N1: U1.GPIO25, DS1.DQ, R1.Pin_0
  N2: U1.GPIO26, LCM1602_IIC1.SCL
  N3: U1.GPIO27, LCM1602_IIC1.SDA
  GND: U1.GND, LCM1602_IIC1.GND, M1.GND
  N4: U1.GPIO13, R2.Pin_0
  N5: U1.GPIO18, S3.Pin_1, S3.Pin_2, S4.Pin_3, S4.Pin_4
  N6: U1.GPIO19, J1.pin2
  N7: U1.GPIO21, M1.SDA
  N8: U1.GPIO22, M1.SCL
  VSS: LCD1.VSS, LCM1602_IIC1.VSS
  VDD: LCD1.VDD, LCM1602_IIC1.VDD
  N9: LCD1.V0, LCM1602_IIC1.V0
  N10: LCD1.RS, LCM1602_IIC1.RS
  N11: LCD1.R/W, LCM1602_IIC1.RW
  N12: LCD1.E, LCM1602_IIC1.E
  N13: LCD1.DB0, LCM1602_IIC1.D0
  N14: LCD1.DB1, LCM1602_IIC1.D1
  N15: LCD1.DB2, LCM1602_IIC1.D2
  N16: LCD1.DB3, LCM1602_IIC1.D3
  N17: LCD1.DB4, LCM1602_IIC1.D4
  N18: LCD1.DB5, LCM1602_IIC1.D5
  N19: LCD1.DB6, LCM1602_IIC1.D6
  N20: LCD1.DB7, LCM1602_IIC1.D7
  N21: LCD1.LED+, LCM1602_IIC1.A
  N22: LCD1.LED-, LCM1602_IIC1.K
  N23: DS1.GND, LED1.cathode
  N24: LCM1602_IIC1.LED_A, LCM1602_IIC1.LED_B
  N25: R2.Pin_1, LED1.anode
  N26: S2.Pin_3, R4.Pin_1
  N27: S3.Pin_3, R3.Pin_1
  N28: S5.Pin_3, R5.Pin_1

custom parts:
  ESP32-38PinWide: Generic 38-Pin ESP32 with wide format (only access to one side of pins on a breadboard) based on Stephen Lilley's HiLetgo ESP-WROOM-32 ESP32 ESP-32S Development Board.
  LCM1602 IIC: I2C-Module to use a 1602 or 2004 LCD on with the wire.h libory Serial LCD Modul
  BME280: Temperature Humidity Barometric presure Sensor
